// Logisim project LPU-1.circ as structural Verilog: 3 circuits, main circuit LPU-1
module LPU_1 (
);

  wire AA, ADD, alu_1_cout, and_1_out, and_2_out, and_3_out, and_4_out, and_5_out, and_7_out,
       bit_extender_1_out, Carry, Carry_q, Clock, controlled_buffer_2_out, controlled_buffer_4_out,
       demultiplexer_1_out1, HLT, JC, JEZ, JMP, LDA, MOV, nor_1_out, nor_2_out, nor_3_out, nor_4_out,
       not_1_out, or_1_out, or_2_out, or_3_out, or_4_out, or_6_out, PC_Clock, PUT, R_Clock, Reset, STA, SUB,
       Zero;
  wire [1:0] controlled_buffer_5_out, Select;
  wire [7:0] A_q, ACC, ACC_I_O, ACC_Out, alu_1_output, B_q, controlled_buffer_6_out, controlled_buffer_8_out,
       Data, or_5_out, or_7_out, R_data, ram_1_data;
  wire [15:0] Address, controlled_buffer_1_out, counter_1_q;
  wire [19:0] ram_2_data;

  or or_1 (or_1_out, Carry, JMP, Zero);
  Counter #(.width(16), .max('hffff), .ongoal("stay")) counter_1 (
    .load(or_1_out), .D(Address), .count(not_1_out), .Q(counter_1_q), .clk(PC_Clock), .clr(Reset));  // open: carry
  not not_1 (not_1_out, or_1_out);
  Button button_1 (.out(Reset));
  or or_2 (or_2_out, STA, LDA);
  assign controlled_buffer_1_out = or_2_out ? Address : 16'bz;  // Controlled_Buffer controlled_buffer_1
  assign controlled_buffer_2_out = STA ? R_Clock : 1'bz;  // Controlled_Buffer controlled_buffer_2
  RAM #(.addrWidth(16), .bus("separate")) ram_1 (
    .addr(controlled_buffer_1_out), .din(ACC_I_O), .data(ram_1_data), .clk(R_Clock),
    .ld(controlled_buffer_2_out));  // open: str, sel, clr
  Decoder decoder_1 (
    .Memory_Input(ram_2_data), .ADD(ADD), .SUB(SUB), .PUT(PUT), .Select_Bits(Select), .JMP(JMP), .JEZ(JEZ),
    .JC(JC), .Data_Bits(Data), .HLT(HLT), .Address_Bits(Address), .MOV(MOV), .LDA(LDA), .STA(STA), .AA(AA));
  RAM #(.addrWidth(16), .dataWidth(20), .bus("asynch")) ram_2 (
    .addr(counter_1_q), .data(ram_2_data));  // open: sel, ld, clr
  assign ACC = LDA ? ram_1_data : 8'bz;  // Controlled_Buffer controlled_buffer_3
  Decoder_part decoder_2 (.out0(PC_Clock), .out1(R_Clock), .sel(and_1_out));  // open: en
  and and_1 (and_1_out, ~HLT, Clock);  // AND_Gate
  Clock clock_1 (.out(Clock));
  assign controlled_buffer_4_out = AA ? R_Clock : 1'bz;  // Controlled_Buffer controlled_buffer_4
  or or_3 (or_3_out, MOV, PUT);
  assign controlled_buffer_5_out = or_3_out ? Select : 2'bz;  // Controlled_Buffer controlled_buffer_5
  assign controlled_buffer_6_out = AA ? ACC_Out : 8'bz;  // Controlled_Buffer controlled_buffer_6
  or or_4 (or_4_out, MOV, PUT);
  assign or_5_out = Data | R_data;  // OR_Gate or_5, 8 bits wide
  assign controlled_buffer_6_out = or_4_out ? or_5_out : 8'bz;  // Controlled_Buffer controlled_buffer_7
  or or_6 (or_6_out, MOV, PUT);
  assign controlled_buffer_8_out = or_6_out ? or_7_out : 8'bz;  // Controlled_Buffer controlled_buffer_8
  assign or_7_out = Data | R_data;  // OR_Gate or_7, 8 bits wide
  Demultiplexer demultiplexer_1 (
    .out0(controlled_buffer_4_out), .out1(demultiplexer_1_out1), .in(R_Clock), .sel(bit_extender_1_out));  // open: en
  Bit_Extender #(.in_width(2), .out_width(1)) bit_extender_1 (.in(controlled_buffer_5_out), .out(bit_extender_1_out));
  Register Accumulator (.D(ACC), .Q(ACC_Out), .clk(R_Clock), .clr(Reset));  // open: en
  DotMatrix #(.inputtype("row"), .matrixcols(8), .matrixrows(1)) dotmatrix_1 (.row0(A_q));
  DotMatrix #(.inputtype("row"), .matrixcols(8), .matrixrows(1)) dotmatrix_2 (.row0(B_q));
  Register A (.D(controlled_buffer_6_out), .Q(A_q), .clk(controlled_buffer_4_out), .clr(Reset));  // open: en
  Register B (.D(controlled_buffer_8_out), .Q(B_q), .clk(demultiplexer_1_out1), .clr(Reset));  // open: en
  Multiplexer #(.width(8)) multiplexer_1 (.in0(A_q), .in1(B_q), .out(R_data), .sel(Select[1]));  // open: en
  Hex_Digit_Display hex_digit_display_1 (.value(ACC_Out[7:4]));  // open: dp
  DotMatrix #(.inputtype("row"), .matrixcols(8), .matrixrows(1)) dotmatrix_3 (.row0(ACC_Out));
  nor nor_1 (nor_1_out, A_q[0], A_q[1]);
  and and_2 (and_2_out, nor_1_out, nor_2_out);
  nor nor_2 (nor_2_out, A_q[2], A_q[3]);
  nor nor_3 (nor_3_out, A_q[4], A_q[5]);
  and and_3 (and_3_out, nor_3_out, nor_4_out);
  nor nor_4 (nor_4_out, A_q[6], A_q[7]);
  ALU alu_1 (.ADD_SUB(SUB), .A(A_q), .B(B_q), .Output(alu_1_output), .Cout(alu_1_cout));
  and and_4 (and_4_out, alu_1_cout, R_Clock);
  Hex_Digit_Display hex_digit_display_2 (.value(ACC_Out[3:0]));  // open: dp
  and and_5 (and_5_out, and_2_out, and_3_out);
  and and_6 (Zero, and_5_out, JEZ);
  assign ACC = SUB ? alu_1_output : 8'bz;  // Controlled_Buffer controlled_buffer_9
  assign ACC = ADD ? alu_1_output : 8'bz;  // Controlled_Buffer controlled_buffer_10
  Register #(.width(1)) u_Carry (.D(alu_1_cout), .Q(Carry_q), .clk(and_4_out), .clr(Reset));  // open: en
  and and_7 (and_7_out, Carry_q, JC);
  assign Carry = JC ? ~and_7_out : 1'bz;  // Controlled_Inverter controlled_inverter_1
endmodule

module ALU (
  input  ADD_SUB,
  input  [7:0] A,
  input  [7:0] B,
  output [7:0] Output,
  output Cout
);

  wire [7:0] xor_1_out;

  xor xor_1 (xor_1_out[0], ADD_SUB, B[0]);
  xor xor_2 (xor_1_out[1], ADD_SUB, B[1]);
  xor xor_3 (xor_1_out[2], ADD_SUB, B[2]);
  xor xor_4 (xor_1_out[3], ADD_SUB, B[3]);
  xor xor_5 (xor_1_out[4], ADD_SUB, B[4]);
  xor xor_6 (xor_1_out[5], ADD_SUB, B[5]);
  xor xor_7 (xor_1_out[6], ADD_SUB, B[6]);
  xor xor_8 (xor_1_out[7], ADD_SUB, B[7]);
  Adder adder_1 (.a(A), .b(xor_1_out), .out(Output), .cin(ADD_SUB), .cout(Cout));
endmodule

module Decoder (
  input  [19:0] Memory_Input,
  output ADD,
  output SUB,
  output PUT,
  output JMP,
  output JEZ,
  output [1:0] Select_Bits,
  output JC,
  output MOV,
  output LDA,
  output [7:0] Data_Bits,
  output STA,
  output AA,
  output HLT,
  output [15:0] Address_Bits
);

  Decoder_part #(.select(4)) decoder_1 (
    .out1(ADD), .out2(SUB), .out3(PUT), .out4(JMP), .out5(JEZ), .out6(JC), .out7(MOV), .out8(LDA),
    .out9(STA), .out10(AA), .out15(HLT), .sel(Memory_Input[3:0]));  // open: out0, out11, out12, out13, out14, en

  assign Address_Bits = Memory_Input[19:4];
  assign Data_Bits = Memory_Input[13:6];
  assign Select_Bits = Memory_Input[5:4];
endmodule
